// Logisim project CPU.circ as structural Verilog: 3 circuits, main circuit main
module main (
);

  wire button_1_out, button_2_out;
  wire [1:0] Program_Logic_instruction_set;
  wire [3:0] Register_Bank_output;
  wire [7:0] Program_Logic_instruction_set_2;

  Button button_1 (.out(button_1_out));
  Button button_2 (.out(button_2_out));
  Register_Bank Register_Bank (
    .Write_Enable(Program_Logic_instruction_set_2[7]), .Read_Select(Program_Logic_instruction_set),
    .Write_Select({Program_Logic_instruction_set_2[3], Program_Logic_instruction_set_2[4]}),
    .Output(Register_Bank_output),
    .Input({{2{Program_Logic_instruction_set_2[0]}}, Program_Logic_instruction_set_2[1], Program_Logic_instruction_set_2[2]}),
    .reset(button_2_out));
  Program_Logic Program_Logic (
    .clock(button_1_out), .reset(button_2_out),
    .instruction_set({Program_Logic_instruction_set_2[7], Program_Logic_instruction_set[0], Program_Logic_instruction_set[1], Program_Logic_instruction_set_2[4:0]}));
  // Probe on Register_Bank_output
  Comparator comparator_1 ();  // open: a, b, gt, eq, lt
endmodule

module Program_Logic (
  input  clock,
  input  reset,
  output [7:0] instruction_set
);

  wire [7:0] adder_1_out, register_1_q;

  Register register_1 (.D(adder_1_out), .Q(register_1_q), .clk(clock), .clr(reset));  // open: en
  Adder adder_1 (.a(register_1_q), .b(8'h1), .out(adder_1_out));  // open: cin, cout
  ROM rom_1 (.addr(register_1_q), .data(instruction_set));  // open: sel

  // Notes on the sheet:
  //   contents of rom_1 (hex, n*v repeats v):
  //   85 0 0 0 85 0 0 0 85 0 0 0 85 0 0 0 85 0 0 0 85 7*0 85 0 0 0 85 0 0 0 85 0 0 0 85 0 0 0 85 0 0 0 85
  //   0 0 0 85 0 0 0 85 0 0 0 85 184*0 11
endmodule

module Register_Bank (
  input  reset,
  input  [3:0] Input,
  input  Write_Enable,
  input  [1:0] Write_Select,
  input  [1:0] Read_Select,
  output [3:0] Output
);

  wire decoder_1_out0, decoder_1_out1, decoder_1_out2, decoder_1_out3;
  wire [3:0] register_1_q, register_2_q, register_3_q, register_4_q;

  Decoder #(.select(2)) decoder_1 (
    .out0(decoder_1_out0), .out1(decoder_1_out1), .out2(decoder_1_out2), .out3(decoder_1_out3),
    .sel(Write_Select), .en(Write_Enable));
  Register #(.width(4), .trigger("high")) register_1 (
    .D(Input), .Q(register_1_q), .clk(decoder_1_out1), .clr(reset));  // open: en
  Register #(.width(4), .trigger("high")) register_2 (
    .D(Input), .Q(register_2_q), .clk(decoder_1_out2), .clr(reset));  // open: en
  Register #(.width(4), .trigger("high")) register_3 (
    .D(Input), .Q(register_3_q), .clk(decoder_1_out0), .clr(reset));  // open: en
  Register #(.width(4), .trigger("high")) register_4 (
    .D(Input), .Q(register_4_q), .clk(decoder_1_out3), .clr(reset));  // open: en
  Multiplexer #(.select(2), .width(4)) multiplexer_1 (
    .in0(register_3_q), .in1(register_1_q), .in2(register_2_q), .in3(register_4_q), .out(Output),
    .sel(Read_Select));  // open: en
endmodule
